// Logisim project Tic_tac_toe_2_players.circ as structural Verilog: 1 circuit, main circuit main
module main (
);

  wire and_1_out, and_2_out, and_3_out, and_4_out, and_5_out, and_6_out, and_7_out, and_8_out, and_9_out,
       and_10_out, and_11_out, and_12_out, and_13_out, and_14_out, and_15_out, and_16_out, and_17_out,
       and_18_out, and_19_out, Awin, button_1_out, Bwin, clock_1_out, DRAW, L1a, L1b, L1c, L1d, L1e, L1f,
       L1g, L1h, L1i, L2a, L2b, L2c, L2d, L2e, L2f, L2g, L2h, L2i, or_1_out, or_2_out, or_3_out, p1a, p1b,
       p1c, p1d, p1e, p1f, p1g, p1h, p1i, p2a, p2b, p2c, p2d, p2e, p2f, p2g, p2h, p2i;

  Clock clock_1 (.out(clock_1_out));
  J_K_Flip_Flop j_k_ff_1 (.J(p1a), .clk(clock_1_out), .K(p2a), .Q(L1a), .reset(button_1_out));  // open: Qn, preset, en
  J_K_Flip_Flop j_k_ff_2 (.J(p1b), .clk(clock_1_out), .K(p2b), .Q(L1b), .reset(button_1_out));  // open: Qn, preset, en
  J_K_Flip_Flop j_k_ff_3 (.J(p1c), .clk(clock_1_out), .K(p2c), .Q(L1c), .reset(button_1_out));  // open: Qn, preset, en
  J_K_Flip_Flop j_k_ff_4 (.J(p1d), .clk(clock_1_out), .K(p2d), .Q(L1d), .reset(button_1_out));  // open: Qn, preset, en
  J_K_Flip_Flop j_k_ff_5 (.J(p1a), .clk(clock_1_out), .K(p2a), .Qn(L2a), .preset(button_1_out));  // open: Q, en, reset
  J_K_Flip_Flop j_k_ff_6 (.J(p1b), .clk(clock_1_out), .K(p2b), .Qn(L2b), .preset(button_1_out));  // open: Q, en, reset
  J_K_Flip_Flop j_k_ff_7 (.J(p1c), .clk(clock_1_out), .K(p2c), .Qn(L2c), .preset(button_1_out));  // open: Q, en, reset
  J_K_Flip_Flop j_k_ff_8 (.J(p1d), .clk(clock_1_out), .K(p2d), .Qn(L2d), .preset(button_1_out));  // open: Q, en, reset
  J_K_Flip_Flop j_k_ff_9 (.J(p1e), .clk(clock_1_out), .K(p2e), .Q(L1e), .reset(button_1_out));  // open: Qn, preset, en
  J_K_Flip_Flop j_k_ff_10 (.J(p1f), .clk(clock_1_out), .K(p2f), .Q(L1f), .reset(button_1_out));  // open: Qn, preset, en
  J_K_Flip_Flop j_k_ff_11 (.J(p1g), .clk(clock_1_out), .K(p2g), .Q(L1g), .reset(button_1_out));  // open: Qn, preset, en
  J_K_Flip_Flop j_k_ff_12 (.J(p1h), .clk(clock_1_out), .K(p2h), .Q(L1h), .reset(button_1_out));  // open: Qn, preset, en
  J_K_Flip_Flop j_k_ff_13 (.J(p1e), .clk(clock_1_out), .K(p2e), .Qn(L2e), .preset(button_1_out));  // open: Q, en, reset
  J_K_Flip_Flop j_k_ff_14 (.J(p1f), .clk(clock_1_out), .K(p2f), .Qn(L2f), .preset(button_1_out));  // open: Q, en, reset
  J_K_Flip_Flop j_k_ff_15 (.J(p1g), .clk(clock_1_out), .K(p2g), .Qn(L2g), .preset(button_1_out));  // open: Q, en, reset
  J_K_Flip_Flop j_k_ff_16 (.J(p1h), .clk(clock_1_out), .K(p2h), .Qn(L2h), .preset(button_1_out));  // open: Q, en, reset
  Button button_1 (.out(button_1_out));
  and and_1 (and_1_out, L2a, L2i);
  and and_2 (and_2_out, L2g, L2c);
  and and_3 (and_3_out, L2d, L2f);
  and and_4 (and_4_out, L2b, L2h);
  and and_5 (and_5_out, L2c, L2b);
  and and_6 (and_6_out, L2g, L2d);
  and and_7 (and_7_out, L2a, L2d);
  and and_8 (and_8_out, L2h, L2i);
  Button button_2 (.out(p1a));
  Button button_3 (.out(p2a));
  Button button_4 (.out(p2b));
  Button button_5 (.out(p1b));
  Button button_6 (.out(p1c));
  Button button_7 (.out(p2c));
  J_K_Flip_Flop j_k_ff_17 (.J(p1i), .clk(clock_1_out), .K(p2i), .Q(L1i), .reset(button_1_out));  // open: Qn, preset, en
  or or_1 (or_1_out, and_1_out, and_2_out, and_3_out, and_4_out);
  or or_2 (or_2_out, and_5_out, and_6_out);
  or or_3 (or_3_out, and_7_out, and_8_out);
  LED led_1 (.in(L1a));
  LED led_2 (.in(L2a));
  LED led_3 (.in(L1b));
  LED led_4 (.in(L2b));
  LED led_5 (.in(L2c));
  LED led_6 (.in(L1c));
  J_K_Flip_Flop j_k_ff_18 (.J(p1i), .clk(clock_1_out), .K(p2i), .Qn(L2i), .preset(button_1_out));  // open: Q, en, reset
  and and_9 (and_9_out, or_1_out, L2e);
  and and_10 (and_10_out, L2a, or_2_out);
  and and_11 (and_11_out, L2g, or_3_out);
  Button button_8 (.out(p1d));
  Button button_9 (.out(p2d));
  LED led_7 (.in(L1d));
  Button button_10 (.out(p1e));
  Button button_11 (.out(p2e));
  LED led_8 (.in(L1e));
  Button button_12 (.out(p1f));
  Button button_13 (.out(p2f));
  LED led_9 (.in(L1f));
  LED led_10 (.in(L2d));
  Button button_14 (.out(p1g));
  Button button_15 (.out(p1h));
  LED led_11 (.in(L2e));
  LED led_12 (.in(L2f));
  Button button_16 (.out(p1i));
  or or_4 (Awin, and_9_out, and_10_out, and_11_out);
  Button button_17 (.out(p2g));
  LED led_13 (.in(L1g));
  LED led_14 (.in(L2g));
  LED led_15 (.in(L2h));
  LED led_16 (.in(L1h));
  Button button_18 (.out(p2h));
  Button button_19 (.out(p2i));
  LED led_17 (.in(L1i));
  LED led_18 (.in(L2i));
  and and_12 (and_12_out, L1a, L1b, L1c);
  and and_13 (and_13_out, L1d, L1e, L1f);
  and and_14 (and_14_out, L1g, L1h, L1i);
  and and_15 (and_15_out, L1a, L1e, L1i);
  and and_16 (and_16_out, L1g, L1e, L1f);
  and and_17 (and_17_out, L1c, L1f, L1i);
  and and_18 (and_18_out, L1a, L1d, L1g);
  and and_19 (and_19_out, L1e, L1b, L1h);
  LED led_19 (.in(Awin));
  LED led_20 (.in(DRAW));
  LED led_21 (.in(Bwin));
  or or_5 (Bwin, and_12_out, and_13_out, and_14_out, and_15_out, and_16_out, and_17_out, and_18_out, and_19_out);
  nor nor_1 (DRAW, Awin, Bwin);

  // Notes on the sheet:
  //   Reset
  //   Draw circuit with simple logic (have error)
endmodule
